# Fritzing sketch RFIDMachineACS_Fritzing_Circuit (saved by Fritzing 0.9.2b)
breadboards: 1

parts:
  U1 = RELAY [package=relay-g5q]
  Q1 = NPN-Transistor [package="TO92 [THT]"]
  R1 = Resistor [tolerance=±5% resistance=1M package=THT]
  Part1 = Intel Edison Arduinobreakout
  J2 = screw terminal, 3 pins
  Grove3 = Grove OLED 128x96
  RFID1 = Parallax RFID Reader Module
  IC2 = IC, DIP package, 14 pins [chip_label=NTE4071B]
  IC1 = IC, DIP package, 16 pins [chip_label=NTE4051B]
  R2 = Resistor [tolerance=±5% resistance=1k package=THT]
  S1 = Toggle Switch [package=THT]

nets:
  VCC: U1.COIL2, Part1.5V, Grove3.VCC, RFID1.VCC, IC2.pin14, IC1.pin16, S1.COM
  N1: U1.MAIN, J2.pin3
  N2: U1.NO, J2.pin2
  N3: U1.NC, J2.pin1
  N4: U1.COIL1, Q1.C
  GND: Q1.E, R1.Pin_1, Part1.GND, Grove3.GND, RFID1.GND, IC2.pin7, IC1.pin6, IC1.pin7, IC1.pin8, IC1.pin9, IC1.pin10, IC1.pin12, R2.Pin_0
  N5: Q1.B, R1.Pin_0, IC2.pin8, IC1.pin14
  N6: Part1.D8, IC2.pin9
  N7: Part1.A4/SDA, Grove3.SDA
  N8: Part1.A5/SCL, Grove3.SCL
  N9: Part1.D0/RX, RFID1.Sout
  N10: Part1.D1/TX, RFID1./ENABLE
  N11: IC2.pin10, IC1.pin11
  N12: IC1.pin13, R2.Pin_1, S1.L2
